# Fritzing sketch electricCircuitSketch (saved by Fritzing 0.9.3b)

parts:
  Arduino_Uno = Arduino Uno (Rev3) - ICSP
  Button_2 = Pushbutton [package="[THT]"]
  Button_3 = Pushbutton [package="[THT]"]
  Button_4 = Pushbutton [package="[THT]"]
  Button_1 = Pushbutton [package="[THT]"]
  R1 = Resistor [tolerance=±5% resistance=220 package=THT]
  R2 = Resistor [tolerance=±5% resistance=220 package=THT]
  R3 = Resistor [tolerance=±5% resistance=220 package=THT]
  R4 = Resistor [tolerance=±5% resistance=220 package=THT]
  BMP280 = Adafruit BMP280 [part_number="Adafruit #2651"]

nets:
  N1: Arduino_Uno.A0, Button_1.Pin_1, Button_1.Pin_2, R1.Pin_0
  N2: Arduino_Uno.A1, Button_2.Pin_1, Button_2.Pin_2, R2.Pin_0
  N3: Arduino_Uno.A2, Button_3.Pin_1, Button_3.Pin_2, R3.Pin_0
  N4: Arduino_Uno.A3, Button_4.Pin_1, Button_4.Pin_2, R4.Pin_0
  5V: Arduino_Uno.5V, Button_2.Pin_3, Button_2.Pin_4, Button_3.Pin_3, Button_3.Pin_4, Button_4.Pin_3, Button_4.Pin_4, Button_1.Pin_3, Button_1.Pin_4, BMP280.VCC
  GND: Arduino_Uno.GND, R1.Pin_1, R2.Pin_1, R3.Pin_1, R4.Pin_1, BMP280.GND
  N5: Arduino_Uno.A4/SDA, BMP280.SDI/SDA
  N6: Arduino_Uno.A5/SCL, BMP280.SCK/SCL

custom parts:
  Adafruit BMP280: Bosch has stepped up their game with their new BMP280 sensor, an environmental sensor with temperature, barometric pressure that is the next generation upgrade to the BMP085/BMP180/BMP183. This sensor is great for all sorts of weather sensing and can even be used in both I2C and SPI! This precision sensor from Bosch is the best low-cost, precision sensing solution for measuring barometric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

// code stored in the sketch: kazoHero.ino
/***************************************************************************
  This is a library for the BMP280 humidity, temperature & pressure sensor

  Designed specifically to work with the Adafruit BMP280 Breakout
  ----> http://www.adafruit.com/products/2651

  These sensors use I2C or SPI to communicate, 2 or 4 pins are required
  to interface.

  Adafruit invests time and resources providing this open source code,
  please support Adafruit andopen-source hardware by purchasing products
  from Adafruit!

  Written by Limor Fried & Kevin Townsend for Adafruit Industries.
  BSD license, all text above must be included in any redistribution
 ***************************************************************************/
+
#include <Wire.h>
#include <SPI.h>
#include <Adafruit_BMP280.h>

Adafruit_BMP280 bmp;

float base;

float get_pressure(bool reset_norm=false) {
    float semple = bmp.readPressure();
    if (reset_norm) {
      base = semple;
    }
    else {
      base = min(semple, base);
    }
    return semple - base;
}

void setup() {
  Serial.begin(9600);
  while ( !Serial ) delay(100);   // wait for native usb
  if (!bmp.begin()) {  
    Serial.println("Could not find a valid BMP280 sensor, check wiring!");
    while (1);
  }

  /* Default settings from datasheet. */
  bmp.setSampling(Adafruit_BMP280::MODE_NORMAL,     /* Operating Mode. */
                  Adafruit_BMP280::SAMPLING_X2,     /* Temp. oversampling */
                  Adafruit_BMP280::SAMPLING_X16,    /* Pressure oversampling */
                  Adafruit_BMP280::FILTER_X16,      /* Filtering. */
                  Adafruit_BMP280::STANDBY_MS_250); /* Standby time. */
  get_pressure(true);
}

void loop() {
//    Serial.print(F("Temperature = "));
//    Serial.print(bmp.readTemperature());
//    Serial.println(" *C");
    double pressure = get_pressure();
    Serial.print(F("Pressure = "));
    Serial.println(pressure);
    Serial.print("1: ");
    Serial.print(digitalRead(A0));
    Serial.print(", 2: ");
    Serial.print(digitalRead(A1));
    Serial.print(", 3: ");
    Serial.print(digitalRead(A2));
    Serial.print(", 4: ");
    Serial.println(digitalRead(A3));

//    Serial.print(F("Approx altitude = "));
//    Serial.print(bmp.readAltitude(1013.25)); /* Adjusted to local forecast! */
//    Serial.println(" m");
    delay(500);  
}
